// Logisim project archiMinimale.circ as structural Verilog: 1 circuit, main circuit main
module main (
  input  H,
  input  Raz
);

  wire beq, bgtz, blez, bne, branch, comparator_3_eq, comparator_4_eq, cv_0, cv_4, emem, ereg, immrt,
       multiplexer_8_out, not_1_out, not_2_out, or_1_out, rsshamt, rtrd, sns, tunnel, ualmem;
  wire [0:0] keyboard_1_avail;
  wire [3:0] op;
  wire [4:0] multiplexer_1_out, num_rd, num_rs, num_rt, shamt;
  wire [5:0] co, nf;
  wire [6:0] keyboard_1_data;
  wire [31:0] adder_1_p1, adder_1_p2, adder_1_p3, bit_extender_1_out, bit_extender_2_out, bit_extender_3_out,
       imm32, mips_ram_1_p7, multiplexer_2_out, multiplexer_3_out, multiplexer_7_out, pc, res, rs, rt, w,
       wmem;

  not not_1 (not_1_out, ereg);
  // PLA pla_1: pin names not known; wires that end beside it: co, {rsshamt, emem, ereg, branch, ualmem, immrt, rtrd}
  // Probe on sns
  // Probe on rtrd
  // Probe on immrt
  // Probe on ualmem
  // Probe on branch
  not not_2 (not_2_out, ereg);
  // Probe on not_2_out
  // Probe on emem
  // Probe on op
  // Probe on shamt
  // Probe on rsshamt
  Multiplexer #(.width(5), .enable("false")) multiplexer_1 (
    .in0(num_rt), .in1(num_rd), .out(multiplexer_1_out), .sel(rtrd));
  // RegisterFile registerfile_1: pin names not known; wires that end beside it: w, H, not_1_out, multiplexer_1_out, num_rs, num_rt, Raz, rs, rt
  Comparator #(.width(32)) comparator_1 (.a(res), .b(32'hffff0000), .eq(cv_4));  // open: gt, lt
  Keyboard keyboard_1 (.clk(H), .re(cv_4), .clr(Raz), .avail(keyboard_1_avail[0]), .data(keyboard_1_data));
  assign bit_extender_1_out = {{27{1'b0}}, shamt};  // Bit_Extender bit_extender_1
  Multiplexer #(.width(32), .enable("false")) multiplexer_2 (
    .in0(imm32), .in1(rt), .out(multiplexer_2_out), .sel(immrt));
  // PLA PLA_2: pin names not known; wires that end beside it: {nf, co}, {sns, op}
  Comparator #(.width(32)) comparator_2 (.a(res), .b(32'hffff0004), .eq(cv_0));  // open: gt, lt
  Multiplexer #(.width(32), .enable("false")) multiplexer_3 (
    .in0(rs), .in1(bit_extender_1_out), .out(multiplexer_3_out), .sel(rsshamt));
  // MIPS_ALU mips_alu_1: pin names not known; wires that end beside it: multiplexer_3_out, multiplexer_2_out, op, tunnel, res
  Multiplexer #(.select(2), .width(32), .enable("false")) multiplexer_4 (
    .in1({{25{1'b0}}, keyboard_1_data}), .in2({{31{1'b0}}, keyboard_1_avail[0]}), .out(wmem),
    .sel({cv_0, cv_4}));  // open: in0, in3
  // MIPSProgramROM mipsprogramrom_1: pin names not known; wires that end beside it: pc, {co, num_rs, num_rt, num_rd, shamt, nf}
  // Probe on {co, num_rs, num_rt, num_rd, shamt, nf}
  Comparator #(.width(32)) comparator_3 (.a(res), .b(32'hffff000c), .eq(comparator_3_eq));  // open: gt, lt
  TTY tty_1 (.data(rt[6:0]), .clk(H), .we(comparator_3_eq), .clr(Raz));
  assign bit_extender_2_out = {{16{num_rd[4]}}, {num_rd, shamt, nf}};  // Bit_Extender bit_extender_2
  Multiplexer #(.width(32), .enable("false")) multiplexer_5 (
    .in0(bit_extender_2_out), .in1(bit_extender_3_out), .out(imm32), .sel(sns));
  assign bit_extender_3_out = {{16{1'b0}}, {num_rd, shamt, nf}};  // Bit_Extender bit_extender_3
  // Probe on res
  // Probe on pc
  // Probe on co
  // Probe on num_rs
  // Probe on rs
  // Probe on num_rt
  // Probe on rt
  // Probe on num_rd
  // Probe on shamt
  // Probe on nf
  // Probe on imm32
  // AND_Gate and_1 has open pins: in0=emem, in1=comparator_4_eq, out=open
  Comparator #(.width(12)) comparator_4 (.a(res[31:20]), .b(12'h80), .eq(comparator_4_eq));  // open: gt, lt
  // MIPS_RAM mips_ram_1: pin names not known; wires that end beside it: res[19:0], rt, emem, 1'b1, H, Raz, mips_ram_1_p7, wmem
  Multiplexer #(.width(32), .enable("false")) multiplexer_6 (.in0(res), .in1(mips_ram_1_p7), .out(w), .sel(ualmem));
  and and_2 (beq, tunnel, branch);
  Multiplexer #(.width(32), .enable("false")) multiplexer_7 (
    .in0(adder_1_p1), .in1(adder_1_p3), .out(multiplexer_7_out), .sel(multiplexer_8_out));
  // Adder adder_1: pin names not known; wires that end beside it: adder_1_p1, adder_1_p2, adder_1_p3
  and and_3 (bne, ~tunnel, branch);  // AND_Gate
  // Adder adder_2: pin names not known; wires that end beside it: 32'h4, pc, adder_1_p1
  Register #(.width(32), .trigger("falling")) register_1 (.D(multiplexer_7_out), .en(1'b1), .Q(pc), .clk(H), .clr(Raz));
  Shifter #(.width(32)) shifter_1 (.in(imm32), .\dist (5'b00010), .out(adder_1_p2));
  Multiplexer #(.select(2), .enable("false")) multiplexer_8 (
    .in0(beq), .in1(bne), .in2(blez), .in3(bgtz), .out(multiplexer_8_out), .sel(co[1:0]));
  and and_4 (blez, or_1_out, branch);
  or or_1 (or_1_out, tunnel, rs[31]);
  and and_5 (bgtz, ~or_1_out, branch);  // AND_Gate

  // Other names for the same wires on the sheet: _0 = Raz

  // Notes on the sheet:
  //   commandes
  //   Meh
  //   Entrées/Sorties
  //   décomposition de l'opération MIPS
  //   vérifications
  //   mémoire de donnée
  //   on suppose que l'on a la valeur de rs UNIQUEMENT si on utilise rd --> ???
  //   détermination de la prochaine instruction (pc)
endmodule
